# Fritzing sketch Project_01_and_Project_02 (saved by Fritzing 0.6.3b)
breadboards: 1

parts:
  R1 = Resistor [tolerance=±5% resistance=220 package=THT]
  LED1 = LED - 5mm [color="Red (633nm)" package="5 mm [THT]"]
  Arduino_ADK = Arduino Mega

nets:
  N1: R1.Pin_0, Arduino_ADK.D2
  N2: R1.Pin_1, LED1.anode
  N3: LED1.cathode, Arduino_ADK.GND
