# Fritzing sketch Project_03 (saved by Fritzing 0.6.3b)
breadboards: 1

parts:
  Arduino_ADK = Arduino Mega
  S1 = Pushbutton [package=THT]
  R1 = Resistor [tolerance=±5% resistance=10k package=THT]

nets:
  N1: Arduino_ADK.GND, S1.leg0
  N2: Arduino_ADK.D2, S1.leg1, R1.Pin_1
  N3: Arduino_ADK.+5V, R1.Pin_0
