# Fritzing sketch Project_06 (saved by Fritzing 0.6.3b)

parts:
  Arduino_Mega_ADK = Arduino Mega
  R1 = Resistor [tolerance=±5% resistance=1M package=THT]
  J1 = Piezo Speaker

nets:
  N1: Arduino_Mega_ADK.GND, R1.Pin_0, J1.pin1
  N2: Arduino_Mega_ADK.A0, R1.Pin_1, J1.pin2
