# Fritzing sketch Project_10 (saved by Fritzing 0.6.3b)

parts:
  Servo = Basic Servo
  Arduino_ADK = Arduino Mega

nets:
  GND: Servo.gnd, Arduino_ADK.GND
  VCC: Servo.vcc, Arduino_ADK.+5V
  N1: Servo.pulse, Arduino_ADK.D2
