# Fritzing sketch Project_11 (saved by Fritzing 0.6.3b)
breadboards: 1

parts:
  Arduino_ADK = Arduino Mega
  M1 = DC Motor
  T1 = NPN-Transistor [package="TO92 [THT]"]

nets:
  N1: Arduino_ADK.D2, T1.B
  N2: Arduino_ADK.+5V, M1.pin_2
  N3: Arduino_ADK.GND, T1.E
  N4: M1.pin_1, T1.C
