# Fritzing sketch Project_12_Button_Circuit (saved by Fritzing 0.6.3b)
breadboards: 1

parts:
  Arduino_ADK = Arduino Mega
  S1 = Pushbutton [package=THT]
  R2 = Resistor [tolerance=±5% resistance=10k package=THT]

nets:
  N1: Arduino_ADK.D4, S1.leg1, R2.Pin_1
  N2: Arduino_ADK.+5V, R2.Pin_0
  N3: Arduino_ADK.GND, S1.leg0
