# Fritzing sketch Project_12_Complete_Circuit (saved by Fritzing 0.6.3b)
breadboards: 1

parts:
  Arduino_ADK = Arduino Mega
  R1 = Resistor [tolerance=±5% resistance=220 package=THT]
  LED1 = LED - 5mm [color="Red (633nm)" package="5 mm [THT]"]
  J1 = Piezo Speaker
  S1 = Pushbutton [package=THT]
  R2 = Resistor [tolerance=±5% resistance=10k package=THT]
  S2 = Tilt Switch [package=THT]
  R3 = Resistor [tolerance=±5% resistance=10k package=THT]

nets:
  N1: Arduino_ADK.D5, S2.Pin_2, R3.Pin_1
  N2: Arduino_ADK.D4, S1.leg1, R2.Pin_1
  N3: Arduino_ADK.D3, J1.pin2
  N4: Arduino_ADK.D2, R1.Pin_0
  N5: Arduino_ADK.+5V, R2.Pin_0, R3.Pin_0
  N6: Arduino_ADK.GND, LED1.cathode, J1.pin1, S1.leg0, S2.Pin_1
  N7: R1.Pin_1, LED1.anode
