# Fritzing sketch Project_12_LED_Circuit (saved by Fritzing 0.6.3b)
breadboards: 1

parts:
  Arduino_ADK = Arduino Mega
  R1 = Resistor [tolerance=±5% resistance=220 package=THT]
  LED1 = LED - 5mm [color="Red (633nm)" package="5 mm [THT]"]

nets:
  N1: Arduino_ADK.D2, R1.Pin_0
  N2: Arduino_ADK.GND, LED1.cathode
  N3: R1.Pin_1, LED1.anode
