# Fritzing sketch Project_13_Complete_Circuit (saved by Fritzing 0.6.3b)
breadboards: 1

parts:
  Arduino_ADK = Arduino Mega
  R1 = Resistor [tolerance=±5% resistance=220 package=THT]
  LED1 = LED - 5mm [color="Red (633nm)" package="5 mm [THT]"]
  J1 = Piezo Speaker
  S1 = Pushbutton [package=THT]
  R2 = Resistor [tolerance=±5% resistance=10k package=THT]
  IR_Detector = NPN-Transistor [package="TO92 [THT]"]
  LED2 = LED - 5mm [color="Infrared (940nm)" package="5 mm [THT]"]
  R3 = Resistor [tolerance=±5% resistance=220 package=THT]
  R4 = Resistor [tolerance=±5% resistance=10k package=THT]

nets:
  N1: Arduino_ADK.D4, S1.leg1, R2.Pin_1
  N2: Arduino_ADK.D3, J1.pin2
  N3: Arduino_ADK.D2, R1.Pin_0
  N4: Arduino_ADK.+5V, R2.Pin_0, R3.Pin_1, R4.Pin_0
  N5: Arduino_ADK.GND, LED1.cathode, J1.pin1, S1.leg0, IR_Detector.E, LED2.cathode
  N6: Arduino_ADK.A0, IR_Detector.C, R4.Pin_1
  N7: R1.Pin_1, LED1.anode
  N8: LED2.anode, R3.Pin_0
