# Fritzing sketch Project_13_IR_Light_Barrier_Circuit (saved by Fritzing 0.6.3b)
breadboards: 1

parts:
  Arduino_ADK = Arduino Mega
  IR_Detector = NPN-Transistor [package="TO92 [THT]"]
  LED2 = LED - 5mm [color="Infrared (940nm)" package="5 mm [THT]"]
  R3 = Resistor [tolerance=±5% resistance=220 package=THT]
  R4 = Resistor [tolerance=±5% resistance=10k package=THT]

nets:
  N1: Arduino_ADK.+5V, R3.Pin_1, R4.Pin_0
  N2: Arduino_ADK.GND, IR_Detector.E, LED2.cathode
  N3: Arduino_ADK.A0, IR_Detector.C, R4.Pin_1
  N4: LED2.anode, R3.Pin_0
